// Logisim project 2ª Avaliação - Circuito Logico - Alex - 1ºADS.circ as structural Verilog: 1 circuit, main circuit main
module main (
  input  S1,
  input  S2,
  output RT,
  output AD,
  output AL
);

  wire and_3_out, and_4_out, not_1_out, not_2_out, not_3_out, not_4_out;

  and and_1 (RT, S1, S2);
  not not_1 (not_1_out, S1);
  not not_2 (not_2_out, S2);
  not not_3 (not_3_out, S1);
  not not_4 (not_4_out, S2);
  and and_2 (AD, not_1_out, not_2_out);
  and and_3 (and_3_out, not_3_out, not_4_out);
  and and_4 (and_4_out, S1, S2);
  or or_1 (AL, and_3_out, and_4_out);
endmodule
