// Logisim project PrimeirosCircuitos - 04.05.2021.circ as structural Verilog: 5 circuits, main circuit main
module main (
  input  A,
  input  B,
  input  C,
  input  D,
  input  E,
  input  F,
  input  G,
  output SAUDE
);

  wire and_1_out, and_2_out, and_3_out, and_4_out, nor_1_out, nor_2_out, not_1_out, not_2_out, not_3_out,
       not_4_out, not_5_out, not_6_out, not_7_out, not_8_out, or_1_out;

  not not_1 (not_1_out, C);
  not not_2 (not_2_out, D);
  not not_3 (not_3_out, B);
  and and_1 (and_1_out, B, not_1_out, not_2_out);
  and and_2 (and_2_out, D, not_3_out);
  not not_4 (not_4_out, A);
  not not_5 (not_5_out, B);
  not not_6 (not_6_out, C);
  not not_7 (not_7_out, D);
  not not_8 (not_8_out, E);
  or or_1 (or_1_out, A, B, C, D, E);
  nor nor_1 (nor_1_out, A, and_1_out);
  nor nor_2 (nor_2_out, A, E, C, and_2_out);
  and and_3 (and_3_out, not_4_out, not_5_out, not_6_out, not_7_out, not_8_out, or_1_out);
  and and_4 (and_4_out, nor_1_out, nor_2_out);
  nor nor_3 (SAUDE, and_3_out, and_4_out);
  LED led_1 (.in(SAUDE));
endmodule

module PrimeiroCircuito (
  input  A,
  input  B,
  input  C,
  output Sa
);

  wire not_1_out, not_2_out, or_1_out, or_2_out, or_3_out;

  not not_1 (not_1_out, A);
  not not_2 (not_2_out, C);
  or or_1 (or_1_out, A, B);
  or or_2 (or_2_out, B, C);
  or or_3 (or_3_out, not_1_out, not_2_out);
  nand nand_1 (Sa, or_1_out, or_2_out, or_3_out);

  // Notes on the sheet:
  //   Primeiro Circuito
endmodule

module SegundoCircuito (
  input  A,
  input  B,
  input  C,
  input  D,
  output Sa,
  output Sb
);

  wire and_1_out, and_2_out, and_3_out, and_4_out, nor_1_out, nor_2_out, not_1_out, not_2_out, not_3_out,
       not_4_out, not_5_out, not_6_out, not_7_out, or_1_out, or_2_out, or_3_out;

  or or_1 (or_1_out, A, B);
  or or_2 (or_2_out, B, C);
  not not_1 (not_1_out, A);
  or or_3 (or_3_out, not_1_out, not_2_out);
  not not_2 (not_2_out, C);
  not not_3 (not_3_out, A);
  and and_1 (and_1_out, not_3_out, B, C);
  and and_2 (and_2_out, A, not_4_out);
  not not_4 (not_4_out, C);
  and and_3 (and_3_out, A, not_5_out);
  not not_5 (not_5_out, C);
  nand nand_1 (Sa, or_1_out, or_2_out, or_3_out);
  nor nor_1 (nor_1_out, and_1_out, and_2_out);
  not not_6 (not_6_out, B);
  and and_4 (and_4_out, not_6_out, not_7_out);
  not not_7 (not_7_out, C);
  nor nor_2 (nor_2_out, B, and_3_out);
  or or_4 (Sb, nor_1_out, and_4_out, nor_2_out);
endmodule

module TerceiroCircuito (
  input  A,
  input  B,
  input  C,
  output Sa,
  output Sb,
  output Sc
);

  wire and_1_out, and_2_out, and_3_out, and_4_out, and_5_out, nand_1_out, nand_2_out, nor_1_out, nor_2_out,
       not_1_out, not_2_out, not_3_out, not_4_out, not_5_out, not_6_out, not_7_out, not_8_out, not_9_out,
       not_10_out, or_1_out, or_2_out, or_3_out;

  not not_1 (not_1_out, A);
  not not_2 (not_2_out, C);
  not not_3 (not_3_out, A);
  not not_4 (not_4_out, C);
  not not_5 (not_5_out, C);
  not not_6 (not_6_out, A);
  not not_7 (not_7_out, A);
  not not_8 (not_8_out, B);
  or or_1 (or_1_out, A, B);
  or or_2 (or_2_out, B, C);
  or or_3 (or_3_out, not_1_out, not_2_out);
  and and_1 (and_1_out, not_3_out, B, C);
  and and_2 (and_2_out, A, not_4_out);
  not not_9 (not_9_out, B);
  not not_10 (not_10_out, C);
  and and_3 (and_3_out, A, not_5_out);
  and and_4 (and_4_out, not_6_out, B);
  nand nand_1 (nand_1_out, A, B);
  nand nand_2 (nand_2_out, not_7_out, not_8_out);
  nand nand_3 (Sa, or_1_out, or_2_out, or_3_out);
  nor nor_1 (nor_1_out, and_1_out, and_2_out);
  and and_5 (and_5_out, not_9_out, not_10_out);
  nor nor_2 (nor_2_out, B, and_3_out);
  nor nor_3 (Sc, and_4_out, nand_1_out, nand_2_out);
  or or_4 (Sb, nor_1_out, and_5_out, nor_2_out);
endmodule

module CircuitoPrincipal (
  input  A,
  input  B,
  input  C,
  output Sa,
  output Sb,
  output Sc,
  output Sd
);

  wire and_1_out, and_2_out, and_3_out, and_4_out, and_5_out, nand_1_out, nand_2_out, nor_1_out, nor_2_out,
       not_1_out, not_2_out, not_3_out, not_4_out, not_5_out, not_6_out, not_7_out, not_8_out, not_9_out,
       not_10_out, not_11_out, not_12_out, not_13_out, not_14_out, not_15_out, not_16_out, or_1_out,
       or_2_out, or_3_out, or_4_out, or_5_out, or_6_out, or_7_out;

  not not_1 (not_1_out, A);
  not not_2 (not_2_out, C);
  not not_3 (not_3_out, A);
  not not_4 (not_4_out, C);
  not not_5 (not_5_out, C);
  not not_6 (not_6_out, A);
  not not_7 (not_7_out, A);
  not not_8 (not_8_out, B);
  not not_9 (not_9_out, B);
  not not_10 (not_10_out, A);
  not not_11 (not_11_out, B);
  not not_12 (not_12_out, A);
  not not_13 (not_13_out, B);
  not not_14 (not_14_out, C);
  or or_1 (or_1_out, A, B);
  or or_2 (or_2_out, B, C);
  or or_3 (or_3_out, not_1_out, not_2_out);
  and and_1 (and_1_out, not_3_out, B, C);
  and and_2 (and_2_out, A, not_4_out);
  not not_15 (not_15_out, B);
  not not_16 (not_16_out, C);
  and and_3 (and_3_out, A, not_5_out);
  and and_4 (and_4_out, not_6_out, B);
  nand nand_1 (nand_1_out, A, B);
  nand nand_2 (nand_2_out, not_7_out, not_8_out);
  or or_4 (or_4_out, A, B, C);
  or or_5 (or_5_out, A, not_9_out, C);
  or or_6 (or_6_out, not_10_out, not_11_out, C);
  or or_7 (or_7_out, not_12_out, not_13_out, not_14_out);
  nand nand_3 (Sa, or_1_out, or_2_out, or_3_out);
  nor nor_1 (nor_1_out, and_1_out, and_2_out);
  and and_5 (and_5_out, not_15_out, not_16_out);
  nor nor_2 (nor_2_out, B, and_3_out);
  nor nor_3 (Sc, and_4_out, nand_1_out, nand_2_out);
  and and_6 (Sd, or_4_out, or_5_out, or_6_out, or_7_out);
  or or_8 (Sb, nor_1_out, and_5_out, nor_2_out);
endmodule
